# Fritzing sketch Kmart-Drone-Connections (saved by Fritzing 0.9.3b)
breadboards: 1

parts:
  Power_plug1 = Power plug
  SW1 = Toggle Switch [package=THT]
  L2 = Resistor [tolerance=±5% resistance=1.6 package=THT]
  U1 = atmega168 [package=dip]
  D1 = LED - 5mm [color="Red (633nm)" package="5 mm [THT]"]
  K1 = Pushbutton [package="[THT]"]
  R1 = Resistor [tolerance=±5% resistance=0 package=THT]
  K2 = Pushbutton [package="[THT]"]
  R18 = Resistor [tolerance=±5% resistance=0 package=THT]
  R2 = Resistor [tolerance=±5% resistance=220 package=THT]
  ANT1 = Antenna
  RV2 = Thumb Joystick [package=joystick]
  R20 = Resistor [tolerance=±5% resistance=0 package=THT]
  U2 = NPN-Transistor [package="TO92 [THT]"]
  R6 = Resistor [tolerance=±5% resistance=0 package=THT]
  3v3 = Power plug
  K3 = Pushbutton [package="[THT]"]  # not connected
  K4 = Pushbutton [package="[THT]"]
  R21 = Resistor [tolerance=±5% resistance=0 package=THT]
  D2 = Rectifier Diode [part_number=1N4001 package="300 mil [THT]"]
  U3 = NPN-Transistor [package="TO92 [THT]"]
  C20 = Tantalum Capacitor [capacitance=1μF package="100 mil [THT, tantalum]"]
  5V = Power plug
  C16 = Ceramic Capacitor [capacitance=100nF package="100 mil [THT, multilayer]"]
  K5 = Pushbutton [package="[THT]"]
  K6 = Pushbutton [package="[THT]"]  # not connected
  K7 = Pushbutton [package="[THT]"]
  K8 = Pushbutton [package="[THT]"]
  R24 = Resistor [tolerance=±5% resistance=220 package=THT]
  R23 = Resistor [tolerance=±5% resistance=220 package=THT]
  RV1 = Thumb Joystick [package=joystick]
  C18 = Ceramic Capacitor [capacitance=100nF package="100 mil [THT, multilayer]"]
  C17 = Ceramic Capacitor [capacitance=100nF package="100 mil [THT, multilayer]"]
  R13 = Resistor [tolerance=±5% resistance=220 package=THT]
  R22 = Resistor [tolerance=±5% resistance=0 package=THT]
  R25 = Resistor [tolerance=±5% resistance=220 package=THT]
  Q1 = NPN-Transistor [package="TO92 [THT]"]
  C4 = Ceramic Capacitor [capacitance=100nF package="100 mil [THT, multilayer]"]
  R5 = Resistor [tolerance=±5% resistance=220 package=THT]
  D4 = Rectifier Diode [part_number=1N4001 package="300 mil [THT]"]
  F1 = Piezo Speaker

nets:
  N1: Power_plug1.VCC, SW1.L1
  GND: Power_plug1.GND, U1.GND, U1.XLAT1, U1.A3, K1.Pin_4, K2.Pin_3, K2.Pin_4, RV2.V+, RV2.H+, RV2.SEL-, 3v3.GND, K4.Pin_3, K4.Pin_4, U3.C, C20.-, K5.Pin_3, K7.Pin_3, K7.Pin_4, K8.Pin_4, RV1.V+, RV1.H+, RV1.SEL-, C18.0, C17.0, Q1.E, C4.1
  N2: SW1.COM, SW1.L2, L2.Pin_0
  N3: L2.Pin_1, D2.anode
  N4: U1.RESET, U1.D0_(RX), ANT1.antenna_lead
  N5: U1.D1_(TX), U2.E
  N6: U1.D2, C18.1
  N7: U1.VCC, RV2.V
  N8: U1.D5_(PWM), RV2.H
  N9: U1.D11_(PWM), R25.Pin_0
  N10: U1.D13, D1.cathode
  N11: U1.AVCC, U1.AREF, RV2.V-, RV1.V, RV1.V-, C17.1, R13.Pin_0, R13.Pin_1
  N12: U1.A1, RV1.H
  N13: U1.A2, RV2.H-, RV1.H-
  N14: D1.anode, R6.Pin_1
  N15: K1.Pin_1, K1.Pin_2, R1.Pin_0, K2.Pin_1, K2.Pin_2, R18.Pin_0
  N16: R1.Pin_1, R2.Pin_1
  N17: RV2.SEL+, R20.Pin_1
  N18: R20.Pin_0, K4.Pin_1, K4.Pin_2, R21.Pin_0
  N19: U2.B, 5V.VCC
  N20: U2.C, 5V.GND
  N21: R6.Pin_0, 3v3.VCC, C16.0
  N22: R21.Pin_1, K5.Pin_1, K5.Pin_2, R22.Pin_0
  N23: D2.cathode, U3.B
  N24: U3.E, C20.+
  N25: K8.Pin_1, R24.Pin_0
  N26: R24.Pin_1, R23.Pin_0
  N27: R23.Pin_1, RV1.SEL+, R22.Pin_1
  N28: R25.Pin_1, Q1.C
  N29: Q1.B, D4.cathode, D4.anode, F1.pin1, F1.pin2
  N30: C4.0, R5.Pin_0, R5.Pin_1
